# Fritzing sketch esp8266_esp_01_ftdi_logic_level_converter_ (saved by Fritzing 0.8.5b)
breadboards: 1

parts:
  Part2 = FTDI Basic Programmer
  Espessif_Serial_Wifi_Modul_1 = ESP8266 ESP01 [part_number=ESP8266 package=THT]
  Part4 = Logic Level Converter
  LED1 = smd LED [color="Red (633nm)" package="0603 [SMD]"]  # not connected
  R1 = Resistor [tolerance=±5% resistance=220 package=THT]

nets:
  N1: Part2.RXI, Part4.RX2_HV
  N2: Part2.TXO, Part4.TX2_HV
  N3: Part2.POWER, Part4.HV
  GND: Part2.GND, Espessif_Serial_Wifi_Modul_1.GND, Part4.GND
  N4: Espessif_Serial_Wifi_Modul_1.RXD, Part4.TX2_LV
  N5: Espessif_Serial_Wifi_Modul_1.TXD, Part4.RX2_LV
  N6: Espessif_Serial_Wifi_Modul_1.VCC, Espessif_Serial_Wifi_Modul_1.CH_PD, Part4.LV
  N7: Espessif_Serial_Wifi_Modul_1.GPIO02, R1.Pin_0

notes:
  From 3.3v
  Bootloader mode when connected to GND

custom parts:
  ESP8266 ESP01: Generic WiFi Module based on the ESP8266 with onboard PCB antenna and UART communications
