# Fritzing sketch esp8266_esp_01_ftdi_logic_level_converter_dht11 (saved by Fritzing 0.8.5b)
breadboards: 1

parts:
  Part2 = FTDI Basic Programmer
  Espessif_Serial_Wifi_Modul_1 = ESP8266 ESP01 [part_number=ESP8266 package=THT]
  Part4 = Logic Level Converter
  DHT1 = DHT11 Humitidy and Temperature Sensor  # not connected
  R1 = Resistor [tolerance=±5% resistance=10k package=THT]

nets:
  N1: Part2.RXI, Part4.RX2_HV
  N2: Part2.TXO, Part4.TX2_HV
  N3: Part2.POWER, Part4.HV
  GND: Part2.GND, Espessif_Serial_Wifi_Modul_1.GND, Espessif_Serial_Wifi_Modul_1.GPIO00, Part4.GND
  N4: Espessif_Serial_Wifi_Modul_1.RXD, Part4.TX2_LV
  N5: Espessif_Serial_Wifi_Modul_1.TXD, Part4.RX2_LV
  N6: Espessif_Serial_Wifi_Modul_1.VCC, Espessif_Serial_Wifi_Modul_1.CH_PD
  N7: Espessif_Serial_Wifi_Modul_1.GPIO02, R1.Pin_0
  N8: Part4.LV, R1.Pin_1

notes:
  From 3.3v

custom parts:
  ESP8266 ESP01: Generic WiFi Module based on the ESP8266 with onboard PCB antenna and UART communications
  DHT11 Humitidy and Temperature Sensor: DHT11 Humidity and Temperature Sensor
